# Fritzing sketch panic-button (saved by Fritzing 0.9.9b)
circuit board: 8.46667cm x 5.64444cm
breadboards: 2

parts:
  U1 = ESP8266 NodeMCU LoLin module
  S1 = Round Pushbutton
  LED1 = LED - 5mm [color="Red (633nm)" current=0.030 package="5 mm [THT]"]
  R1 = Resistor [tolerance=±5% resistance=10k package="2512 [SMD]"]

nets:
  N1: U1.D1, LED1.anode, R1.Pin_0
  N2: U1.GND, LED1.cathode
  N3: U1.VU, S1.leg1
  N4: S1.leg0, R1.Pin_1

custom parts:
  ESP8266 NodeMCU LoLin module: ESP8266 based NodeMCU
